// Logisim project RSC.circ as structural Verilog: 16 circuits, main circuit main
module main (
  input  NotFlushSEL,
  input  PC_XM_30,
  input  RESET_PC_BIOS,
  input  PC_FD_30,
  input  NOP_FLUSHING
);

  wire AFrwd1, AFrwd2, ALUSel, BFrwd2, bios_1_p6, BrSel, CSRSel, CSRWen, dmem_1_p4, Flush, load_1_p3, MemRW,
       ready_to_receive, reg_1_p6, reg_1_p7, RegWE, store_1_p4, store_1_p5, store_1_p6, store_2_p4,
       store_2_p5, store_2_p6, uart_read_1_p2, write_valid;
  wire [1:0] ASel, BSel, PCSel, uart_write_1_p3;
  wire [1:1] InstSel;
  wire [2:0] WBSel;
  wire [4:0] reg_1_p2;
  wire [7:0] multiplexer_5_out;
  wire [13:0] adder_1_out, adder_2_out, adder_3_out, adder_4_out, adder_5_out, cycle_counter_q,
       Inst_counter_q, multiplexer_1_out, multiplexer_2_out, PC_FD_q, PC_W_q;
  wire [13:1] undriven, undriven_2;
  wire [31:0] A_q, ALU_RESULT_q, B_q, bios_1_p5, BrTaken, BrTaken_xm_q, imem_1_b_dout, Imm_q,
       immediate_1_imm, ImmSel, Inst_W_q, Inst_XM_q, multiplexer_3_out, multiplexer_4_out, multiplexer_6_out,
       multiplexer_7_out, multiplexer_9_out, multiplexer_10_out, multiplexer_11_out, PC_XM_q, reg_1_p1,
       store_1_p1, store_1_p2;

  Adder #(.width(14)) adder_1 (.a(14'h4), .b(PC_FD_q), .out(adder_1_out));  // open: cin, cout
  Adder #(.width(14)) adder_2 (.a(PC_FD_q), .b(immediate_1_imm[13:0]), .out(adder_2_out));  // open: cin, cout
  Multiplexer #(.select(2), .width(14)) multiplexer_1 (
    .in0(adder_1_out), .in1(ALU_RESULT_q[13:0]), .in2(adder_2_out), .in3({undriven, RESET_PC_BIOS}),
    .out(multiplexer_1_out), .sel(PCSel));
  Multiplexer multiplexer_2 (
    .in0(multiplexer_1_out[0]), .in1(store_1_p1[0]), .out(multiplexer_2_out[0]), .sel(BrTaken[0]));
  Register #(.width(14)) PC_FD (.D(multiplexer_2_out), .Q(PC_FD_q));  // open: en, clk, clr
  // store store_1: pin names not known; wires that end beside it: store_1_p1, store_1_p2, PC_XM_30, store_1_p4, store_1_p5, store_1_p6
  IMEM imem_1 (
    .A_wbe(store_1_p5), .A_din(store_1_p4), .A_addr(store_1_p6), .B_addr(multiplexer_2_out[0]),
    .B_dout(imem_1_b_dout));  // open: B_din, B_wbe, clk, A_dout
  // BIOS bios_1: pin names not known; wires that end beside it: multiplexer_2_out, 1'b0, store_1_p1, 1'b0, bios_1_p5, bios_1_p6
  Multiplexer #(.select(2), .width(32)) multiplexer_3 (
    .in0(imem_1_b_dout), .in2(bios_1_p5), .out(multiplexer_3_out), .sel({InstSel[1], PC_FD_30}));  // open: in1, in3
  Multiplexer multiplexer_4 (.in0(ALU_RESULT_q[0]), .out(multiplexer_4_out[0]), .sel(CSRSel));  // open: in1
  Register #(.width(32)) CSR_51E (.D(multiplexer_4_out), .en(CSRWen));  // open: clk, Q, clr
  FD_logic fd_logic_1 ();  // open: InstFd, PCFd, InstSel, ImmSell
  // Reg reg_1: pin names not known; wires that end beside it: reg_1_p1, reg_1_p2, multiplexer_3_out[19:15], multiplexer_3_out[31:20], RegWE, reg_1_p6, reg_1_p7
  immediate immediate_1 (.Instruc(multiplexer_3_out), .ImmSel(ImmSel), .Imm(immediate_1_imm));
  Register PC_XM (.D(PC_FD_q[7:0]), .Q(PC_XM_q[7:0]));  // open: en, clk, clr
  Register A (.D(multiplexer_5_out), .Q(A_q[7:0]));  // open: en, clk, clr
  Multiplexer multiplexer_5 (.in0(reg_1_p6), .in1(reg_1_p1[0]), .out(multiplexer_5_out[0]), .sel(AFrwd2));
  Register #(.width(32)) B (.D(multiplexer_6_out), .Q(B_q));  // open: en, clk, clr
  Multiplexer multiplexer_6 (.in0(reg_1_p7), .in1(reg_1_p1[0]), .out(multiplexer_6_out[0]), .sel(BFrwd2));
  Register #(.width(32)) Imm (.D(immediate_1_imm), .Q(Imm_q));  // open: en, clk, clr
  Register #(.width(32)) Inst_XM (.D(multiplexer_3_out), .Q(Inst_XM_q));  // open: en, clk, clr
  Multiplexer #(.width(32)) multiplexer_7 (.in0(A_q), .in1(reg_1_p1), .out(multiplexer_7_out), .sel(AFrwd1));
  Multiplexer #(.width(32)) multiplexer_8 (.in0(B_q), .in1(reg_1_p1), .out(store_1_p2), .sel(BFrwd2));
  Multiplexer multiplexer_9 (.in0(Inst_XM_q[0]), .in1(NOP_FLUSHING), .out(multiplexer_9_out[0]), .sel(Flush));
  Multiplexer #(.select(2), .width(32)) multiplexer_10 (
    .in0(multiplexer_7_out), .in1(PC_XM_q), .out(multiplexer_10_out), .sel(ASel));  // open: in2, in3
  Multiplexer #(.select(2), .width(32)) multiplexer_11 (
    .in0(store_1_p2), .in1(Imm_q), .out(multiplexer_11_out), .sel(BSel));  // open: in2, in3
  Branch branch_1 (.A(multiplexer_7_out), .B(store_1_p2), .BrSel(BrSel), .BrTaken(BrTaken[0]));
  Forwarding forwarding_1 (.Inst_XM(multiplexer_9_out[0]));  // open: Inst_FD, Inst_W, AFrwd1, BFrwd1, AFrwd2, BFrwd2
  XM_logic xm_logic_1 (.InstXm(multiplexer_9_out[0]));  // open: BrSel, ASel, BSel, MemRW, IMemWE, ALUSel, UART_write_valid, UART_ready_to_receive
  ALU alu_1 (.A(multiplexer_10_out), .B(multiplexer_11_out), .ALUSel(ALUSel), .result(store_1_p1));
  Comparator comparator_1 (.a(store_1_p1[7:0]), .b(8'h4), .eq(ready_to_receive));  // open: gt, lt
  Comparator comparator_2 (.a(store_1_p1[7:0]), .b(8'h8), .eq(write_valid));  // open: gt, lt
  // store store_2: pin names not known; wires that end beside it: store_1_p1, store_1_p2, MemRW, store_2_p4, store_2_p5, store_2_p6
  Register PC_W (.D(PC_XM_q[7:0]), .Q(PC_W_q[7:0]));  // open: en, clk, clr
  Register #(.width(32)) ALU_RESULT (.D(store_1_p1), .Q(ALU_RESULT_q));  // open: en, clk, clr
  Register #(.width(32)) Inst_W (
    .D(multiplexer_9_out), .Q({Inst_W_q[31:12], reg_1_p2, Inst_W_q[6:0]}));  // open: en, clk, clr
  Register #(.width(32)) BrTaken_xm (.D(BrTaken), .Q(BrTaken_xm_q));  // open: en, clk, clr
  // DMEM dmem_1: pin names not known; wires that end beside it: store_2_p4, store_2_p5, store_2_p6, dmem_1_p4
  // UART_read uart_read_1: pin names not known; wires that end beside it: ready_to_receive, uart_read_1_p2, uart_write_1_p3[1]
  // UART_write uart_write_1: pin names not known; wires that end beside it: store_1_p2, write_valid, uart_write_1_p3[0]
  Adder #(.width(14)) adder_3 (.a(14'h4), .b(PC_W_q), .out(adder_3_out));  // open: cin, cout
  Register cycle_counter (.D(adder_4_out[7:0]), .Q(cycle_counter_q[7:0]));  // open: en, clk, clr
  Register Inst_counter (.D(adder_5_out[7:0]), .Q(Inst_counter_q[7:0]));  // open: en, clk, clr
  // load load_1: pin names not known; wires that end beside it: ALU_RESULT_q, dmem_1_p4, load_1_p3
  // W_logic w_logic_1: pin names not known; wires that end beside it: BrTaken_xm_q
  Adder #(.width(14)) adder_4 (.a(14'h1), .b(cycle_counter_q), .out(adder_4_out));  // open: cin, cout
  Adder #(.width(14)) adder_5 (
    .a({undriven_2, NotFlushSEL}), .b(Inst_counter_q), .out(adder_5_out));  // open: cin, cout
  Multiplexer #(.select(3)) multiplexer_12 (
    .in0(load_1_p3), .in1(ALU_RESULT_q[0]), .in2(adder_3_out[0]), .in3(uart_read_1_p2),
    .in4(uart_write_1_p3[0]), .in5(cycle_counter_q[0]), .in6(Inst_counter_q[0]), .in7(bios_1_p6),
    .out(reg_1_p1[0]), .sel(WBSel));
  // Pins of 1 and 32 bits meet at ImmSel
  // Pins of 1 and 2 bits meet at ASel
  // Pins of 1 and 2 bits meet at BSel
  // Pins of 1 and 32 bits meet at BrTaken
  // Pins of 8 and 32 bits meet at 32'h80000004
  // Pins of 8 and 32 bits meet at 32'h80000008
  // Pins of 1 and 32 bits meet at {{30{1'b0}}, uart_write_1_p3}
  // Pins of 1 and 14 bits meet at {undriven_2, NotFlushSEL}
  // Pins of 1 and 3 bits meet at WBSel
  // Pins of 1 and 14 bits meet at {undriven, RESET_PC_BIOS}
  // Pins of 1 and 2 bits meet at PCSel
  // Pins of 1 and 2 bits meet at {InstSel[1], PC_FD_30}

  // Other names for the same wires on the sheet: IMemWE = PC_XM_30; InstSel[0] = PC_FD_30

  // Notes on the sheet:
  //   jal & branch predict taken
  //   alu
  //   pc+4
  //   alu_w
  //   alu_xm
  //   RESET MIGHT NOT WORK IF TWO MANY BRANCHS
  //   A_wbe = must be store && PC_XM[30] == 1 && addr[31-29] == 001
  //   NEED BOTH RS1 AND IMM HERE SO NEED TO CHANGE CSRSEL, make the alu result to either rs1 or imm so we don't need csrsel
  //   IF CSRW || CSRWI
  //   ALSO NEED TO MAKE SURE IT IS LOAD/STORE
  //   opcode might not be needed
  //   COUNTER RESET LOGIC MISSING
endmodule

module IMEM (
  input  A_wbe,
  input  A_din,
  input  A_addr,
  input  B_din,
  input  B_addr,
  input  B_wbe,
  input  clk,
  output [31:0] A_dout,
  output [31:0] B_dout
);
endmodule

module Reg (
  input  DataD,
  input  AddrD,
  input  AddrA,
  input  AddrB,
  input  clk,
  input  RegWE,
  output [31:0] DataA,
  output [31:0] DataB
);
endmodule

module DMEM (
  input  [31:0] din,
  input  wbe,
  input  [13:0] addr,
  input  clk,
  output [31:0] dout
);
endmodule

module ALU (
  input  [31:0] A,
  input  [31:0] B,
  input  ALUSel,
  output [31:0] result
);
endmodule

module Branch (
  input  [31:0] A,
  input  [31:0] B,
  input  BrSel,
  output BrTaken
);
endmodule

module immediate (
  input  [31:0] Instruc,
  input  [31:0] ImmSel,
  output [31:0] Imm
);
endmodule

module Forwarding (
  input  Inst_FD,
  input  Inst_XM,
  input  Inst_W,
  output AFrwd1,
  output BFrwd1,
  output AFrwd2,
  output BFrwd2
);
endmodule

module FD_logic (
  input  InstFd,
  input  PCFd,
  output InstSel,
  output ImmSell
);
endmodule

module BIOS (
  input  A_din,
  input  A_addr,
  input  A_wbe,
  input  B_din,
  input  B_addr,
  input  B_wbe,
  input  clk,
  output [31:0] A_dout,
  output [31:0] B_dout
);
endmodule

module UART_read (
  input  ready_recieve,
  output [13:0] read,
  output [31:0] read_valid
);
endmodule

module UART_write (
  input  [13:0] write,
  input  [31:0] write_valid,
  output ready_to_write
);
endmodule

module load (
  input  addr,
  input  mem_data,
  input  func3,
  input  opcode,
  output load_data
);
endmodule

module store (
  input  addr,
  input  din,
  input  func3_xm,
  input  we,
  output store_data,
  output MemRW4,
  output mem_addr
);
endmodule

module XM_logic (
  input  InstXm,
  output BrSel,
  output ASel,
  output BSel,
  output MemRW,
  output IMemWE,
  output ALUSel,
  output UART_write_valid,
  output UART_ready_to_receive
);
endmodule

module W_logic (
  input  InstW,
  input  InstFd,
  input  BrTaken,
  input  BIOSRest,
  output PCSel,
  output Flush,
  output RegWEn,
  output CSRWen,
  output WBSel
);
endmodule
